# Fritzing sketch simon_module (saved by Fritzing 0.9.3b)
breadboards: 1

parts:
  Componente1 = Arduino Uno (Rev3)
  LED1 = smd LED [color="Red (633nm)" package="1206 [SMD]"]
  LED2 = smd LED [color="Red (633nm)" package="1206 [SMD]"]
  LED3 = RGB LED (com. cathode, rbg) [package="5 mm [THT]"]
  LED4 = RGB LED (com. cathode, rbg) [package="5 mm [THT]"]
  R1 = Resistor [tolerance=±5% resistance=220 package="0603 [SMD]"]
  R2 = Resistor [tolerance=±5% resistance=220 package="0603 [SMD]"]
  R3 = Resistor [tolerance=±5% resistance=220 package="0603 [SMD]"]
  R4 = Resistor [tolerance=±5% resistance=220 package="0603 [SMD]"]
  R5 = Resistor [tolerance=±5% resistance=220 package="0603 [SMD]"]
  S1 = Momentary Switch [package=ksa_sealed_tac_switch]
  S2 = Momentary Switch [package=ksa_sealed_tac_switch]
  S3 = Momentary Switch [package=ksa_sealed_tac_switch]
  S4 = Momentary Switch [package=ksa_sealed_tac_switch]

nets:
  N1: Componente1.A3, R2.Pin_1
  N2: Componente1.A4/SDA, R1.Pin_1
  N3: Componente1.A5/SCL, Componente1.D12/MISO, Componente1.D0/RX, Componente1.D1/TX, S1.2, S1.4, S2.2, S2.4, S3.2, S3.4, S4.2
  N4: Componente1.D11_PWM/MOSI, R5.Pin_1
  N5: Componente1.D13/SCK, Componente1.GND, LED1.cathode, LED2.cathode, LED3.common_cathode, LED4.common_cathode, S4.4
  N6: Componente1.D6_PWM, R3.Pin_1
  N7: Componente1.D7, R4.Pin_1
  N8: LED1.anode, R1.Pin_0
  N9: LED3.red_anode, R4.Pin_0
  N10: LED3.blue_anode, R3.Pin_0
  N11: LED4.blue_anode, R5.Pin_0

notes:
  GND bridge
  Blue
  Purple
  Green
  VCC Bridge
